// Logisim project fetch.circ as structural Verilog: 1 circuit, main circuit main
module main (
  output [31:0] out_1
);

  wire clock_1_out;
  wire [31:0] adder_1_out;

  Register #(.width(32)) register_1 (.D(adder_1_out), .Q(out_1), .clk(clock_1_out));  // open: en, clr
  Clock clock_1 (.out(clock_1_out));
  Adder #(.width(32)) adder_1 (.a(out_1), .b(32'h4), .out(adder_1_out));  // open: cin, cout
  ROM #(.addrWidth(24), .dataWidth(32)) rom_1 (.addr(out_1[23:0]));  // open: data, sel
endmodule
